// Logisim project 3_projeto_IAC.circ as structural Verilog: 1 circuit, main circuit main
module main (
);

  wire clock_1_out, decoder_1_out2, decoder_1_out3;
  wire [6:0] R1_q;
  wire [7:0] adder_1_out, adder_2_out, bit_extender_1_out, counter_1_q, multiplexer_1_out, multiplexer_2_out,
       multiplexer_3_out, multiplexer_4_out, multiplexer_5_out, multiplexer_6_out, not_1_out, rom_1_data,
       subtractor_1_out;
  wire [7:7] R1_q_2;

  Clock clock_1 (.out(clock_1_out));
  Counter counter_1 (.clk(clock_1_out), .Q(counter_1_q));  // open: clr, load, up, count, D, carry
  ROM rom_1 (.addr(counter_1_q), .data(rom_1_data));
  Decoder #(.select(2)) decoder_1 (
    .out0(clock_1_out), .out2(decoder_1_out2), .out3(decoder_1_out3), .sel(rom_1_data[7:6]));  // open: out1, en
  assign bit_extender_1_out = {{2{rom_1_data[5]}}, rom_1_data[5:0]};  // Bit_Extender bit_extender_1
  Adder adder_1 (.a({R1_q_2[7], R1_q}), .b(bit_extender_1_out), .out(adder_1_out));  // open: cin, cout
  Multiplexer #(.width(8)) multiplexer_1 (
    .in0(adder_1_out), .in1(subtractor_1_out), .out(multiplexer_1_out), .sel(decoder_1_out2));
  Subtractor subtractor_1 (.a({R1_q_2[7], R1_q}), .b(bit_extender_1_out), .out(subtractor_1_out));  // open: bin, bout
  assign not_1_out = ~{R1_q_2[7], R1_q};  // NOT_Gate not_1, 8 bits wide
  Multiplexer #(.width(8)) multiplexer_2 (
    .in0({R1_q_2[7], R1_q}), .in1({8{1'b0}}), .out(multiplexer_2_out), .sel(R1_q_2[7]));
  Adder adder_2 (.a(not_1_out), .b(8'h1), .out(adder_2_out));  // open: cin, cout
  Multiplexer #(.width(8)) multiplexer_3 (
    .in0({R1_q_2[7], R1_q}), .in1(adder_2_out), .out(multiplexer_3_out), .sel(R1_q_2[7]));
  Multiplexer #(.width(8)) multiplexer_4 (
    .in0(multiplexer_3_out), .in1(multiplexer_2_out), .out(multiplexer_4_out), .sel(rom_1_data[5]));
  Multiplexer #(.width(8)) multiplexer_5 (
    .in0(multiplexer_1_out), .in1(multiplexer_4_out), .out(multiplexer_5_out), .sel(decoder_1_out3));
  Multiplexer #(.width(8)) multiplexer_6 (
    .in0(multiplexer_5_out), .in1(bit_extender_1_out), .out(multiplexer_6_out), .sel(clock_1_out));
  Register R1 (.D(multiplexer_6_out), .en(1'b1), .clk(clock_1_out), .Q({R1_q_2[7], R1_q}));  // open: clr

  // Notes on the sheet:
  //   contents of rom_1 (hex, n*v repeats v):
  //   3 42 86 60 c0 e0
endmodule
